// Logisim project mimo_v05a_OR_EVO.circ as structural Verilog: 12 circuits, main circuit MiMo_v05
// address
module MiMo_v05 (
  input  Cycle,
  input  Stop,
  input  Instr,
  input  [15:0] Addr,
  output [7:0] ucounter
);

  wire ADDR_DEC_fswrite, and_1_out, and_2_out, and_5_out, and_7_out, button_1_out, c, Clear_out,
       Clear_Screen_out, clear_video_out, CLK, CLKIN, cont, FB_LED, fpu_1_nanerror, fpu_1_zero, fpuenable,
       fsload, fswrite, isWrite, multiplexer_4_out, n, Ncmd, not_1_out, not_2_out, or_1_out, RAMSel, reset,
       RGB_video, rgb_video_1_p4, rgb_video_1_p7, rgb_video_2_p3, TTYSel, twrite, z;
  wire [1:0] addrsel, cond;
  wire [2:0] dregs, sregs, tregs;
  wire [3:0] aluop, fsselADDR, icycles, showhexa_1_digit, showhexa_1_out_2, showhexa_1_out_3,
       showhexa_1_out_5, showhexa_2_digit, showhexa_2_out_2, showhexa_2_out_3, showhexa_2_out_5;
  wire [6:0] opcode, xor_1_out;
  wire [7:0] adder_1_out, multiplexer_3_out, multiplexer_5_out;
  wire [15:0] address, aluout, cmds, cycles, data, dreg, DROM, fpu_1_resultd0, fpu_1_resultd1, fpu_1_s0,
       fpu_1_s1, fpu_1_s2, fpu_1_s3, fpu_1_s4, fpu_1_s5, fpu_1_s6, fpu_1_s7, fpu_1_s8, fpu_1_s9, fpu_1_s10,
       fpu_1_s11, fpu_1_s12, fpu_1_s13, fpu_1_s14, fpu_1_s15, frame_buffer_16x16_1_out_6,
       frame_buffer_16x16_1_out_7, frame_buffer_16x16_1_out_8, frame_buffer_16x16_1_out_9,
       frame_buffer_16x16_1_out_10, frame_buffer_16x16_1_out_11, frame_buffer_16x16_1_out_12,
       frame_buffer_16x16_1_out_13, frame_buffer_16x16_1_out_14, frame_buffer_16x16_1_out_15,
       frame_buffer_16x16_1_out_16, frame_buffer_16x16_1_out_17, frame_buffer_16x16_1_out_18,
       frame_buffer_16x16_1_out_19, frame_buffer_16x16_1_out_20, frame_buffer_16x16_1_out_21, fsreg, immed,
       irreg, multiplexer_2_out, multiplexer_6_out, multiplexer_7_out, multiplexer_8_out, pcreg,
       registerfile_1_r0, registerfile_1_r1, registerfile_1_r2, registerfile_1_r3, registerfile_1_r4,
       registerfile_1_r5, registerfile_1_r6, registerfile_1_r7, sreg, treg;
  wire [31:0] fpmultiplier_1_out, fpu_1_d0, fpu_1_d1, fpu_1_d2, fpu_1_d3, fpu_1_d4, fpu_1_d5, fpu_1_d6,
       fpu_1_d7, inttofp_1_p2;
  wire [31:4] CROM;

  Hex_Digit_Display hex_digit_display_1 (.value(showhexa_1_out_2));  // open: dp
  ShowHexa showhexa_1 (
    .Data(address), .Digit(showhexa_1_digit), .out_5(showhexa_1_out_5), .out_2(showhexa_1_out_2),
    .out_3(showhexa_1_out_3));
  RAM #(.addrWidth(14), .asyncread("true"), .dataWidth(16), .databus("bidir")) ram_1 (
    .addr(address[13:0]), .we(and_2_out), .oe(and_1_out), .clk(CLK));  // open: data
  nor nor_1 (Ncmd, ucounter[0], ucounter[1], ucounter[2], ucounter[3], ucounter[5], ucounter[6], ucounter[7], ucounter[4]);
  Hex_Digit_Display hex_digit_display_2 (.value(showhexa_1_digit));  // open: dp
  Hex_Digit_Display hex_digit_display_3 (.value(showhexa_1_out_3));  // open: dp
  and and_1 (and_1_out, RAMSel, not_1_out);
  not not_1 (not_1_out, CROM[6]);
  and and_2 (and_2_out, RAMSel, CROM[6]);
  Address_Decoder ADDR_DEC (
    .enable(1'b1), .Address(address), .RAM(RAMSel), .FB_LED(FB_LED), .RGB_video(RGB_video),
    .fssel(fsselADDR), .fswrite(ADDR_DEC_fswrite), .fpuenable(fpuenable), .TTY(TTYSel));
  // Probe on ucounter
  // Probe on ucounter
  Register Microcounter (.D(adder_1_out), .Q(ucounter), .clk(CLK), .clr(reset));  // open: en
  Clock SysClk (.out(CLKIN));
  Hex_Digit_Display hex_digit_display_4 (.value(showhexa_1_out_5));  // open: dp
  ROM #(.dataWidth(32)) rom_1 (.addr(ucounter), .data({CROM[31:19], cond, CROM[16:9], addrsel, CROM[6:4], aluop}));
  ROM #(.dataWidth(16)) rom_2 (.addr(ucounter), .data(DROM));
  Hex_Digit_Display hex_digit_display_5 (.value(showhexa_2_out_2));  // open: dp
  ShowHexa showhexa_2 (
    .Data(data), .Digit(showhexa_2_digit), .out_5(showhexa_2_out_5), .out_2(showhexa_2_out_2),
    .out_3(showhexa_2_out_3));
  // Probe on opcode
  // Probe on address
  Multiplexer #(.select(2), .width(16)) multiplexer_1 (
    .in0(pcreg), .in1(immed), .in2(aluout), .in3(sreg), .out(address), .sel(addrsel));
  Hex_Digit_Display hex_digit_display_6 (.value(showhexa_2_out_3));  // open: dp
  Hex_Digit_Display hex_digit_display_7 (.value(showhexa_2_digit));  // open: dp
  assign data = CROM[6] ? multiplexer_2_out : 16'bz;  // Controlled_Buffer controlled_buffer_1
  Multiplexer #(.select(2), .width(16)) multiplexer_2 (
    .in0(pcreg), .in1(dreg), .in2(treg), .in3(aluout), .out(multiplexer_2_out), .sel(CROM[21:20]));
  // Probe on CROM[21:20]
  and and_3 (fswrite, ADDR_DEC_fswrite, isWrite);
  and and_4 (fsload, ADDR_DEC_fswrite, not_2_out);
  not not_2 (not_2_out, isWrite);
  or or_1 (or_1_out, z, n);
  // Probe on cond
  // Probe on addrsel
  Hex_Digit_Display hex_digit_display_8 (.value(showhexa_2_out_5));  // open: dp
  // Probe on DROM[7:0]
  Multiplexer #(.width(8)) multiplexer_3 (
    .in0(DROM[7:0]), .in1(DROM[15:8]), .out(multiplexer_3_out), .sel(multiplexer_4_out));
  // Probe on DROM[15:8]
  Multiplexer #(.select(2)) multiplexer_4 (
    .in0(z), .in1(or_1_out), .in2(n), .in3(c), .out(multiplexer_4_out), .sel(cond));
  Multiplexer #(.width(8)) multiplexer_5 (
    .in0({8{1'b0}}), .in1({1'b0, opcode}), .out(multiplexer_5_out), .sel(CROM[19]));
  Multiplexer #(.width(16)) multiplexer_6 (.in0(data), .in1(fsreg), .out(multiplexer_6_out), .sel(fsload));
  // Probe on adder_1_out
  Adder adder_1 (.a(multiplexer_3_out), .b(multiplexer_5_out), .out(adder_1_out));  // open: cin, cout
  Button u_Reset (.out(reset));
  // Probe on multiplexer_6_out
  // Probe on pcreg
  PC pc_1 (
    .imreg(immed), .sreg(sreg), .pcsel(CROM[10:9]), .pcload(CROM[11]), .clock(CLK), .reset(reset),
    .pcout(pcreg));
  // Probe on immed
  ImmediateReg immediatereg_1 (.IMLoad(CROM[14]), .CLKin(CLK), .DataIn(data), .ImmOut(immed));
  InstructionReg instructionreg_1 (
    .reset(reset), .irload(CROM[13]), .instruction(data), .clock(CLK), .dregsel(dregs), .sregsel(sregs),
    .tregsel(tregs), .opcode(opcode), .Instruction_register_Content(irreg));
  // Probe on irreg
  // Probe on opcode
  // Probe on ucounter
  // Probe on CROM[21:20]
  LED led_1 (.in(CROM[22]));
  Frame_Buffer_16x16 frame_buffer_16x16_1 (
    .address(address[3:0]), .store(and_5_out), .data(data), .clock(CLK), .reset(Clear_out),
    .out_6(frame_buffer_16x16_1_out_6), .out_7(frame_buffer_16x16_1_out_7),
    .out_8(frame_buffer_16x16_1_out_8), .out_9(frame_buffer_16x16_1_out_9),
    .out_10(frame_buffer_16x16_1_out_10), .out_11(frame_buffer_16x16_1_out_11),
    .out_12(frame_buffer_16x16_1_out_12), .out_13(frame_buffer_16x16_1_out_13),
    .out_14(frame_buffer_16x16_1_out_14), .out_15(frame_buffer_16x16_1_out_15),
    .out_16(frame_buffer_16x16_1_out_16), .out_17(frame_buffer_16x16_1_out_17),
    .out_18(frame_buffer_16x16_1_out_18), .out_19(frame_buffer_16x16_1_out_19),
    .out_20(frame_buffer_16x16_1_out_20), .out_21(frame_buffer_16x16_1_out_21));
  and and_5 (and_5_out, FB_LED, CROM[6]);
  // Probe on multiplexer_7_out
  Multiplexer #(.select(2), .width(16)) multiplexer_7 (
    .in0(multiplexer_6_out), .in1(immed), .in2(aluout), .in3(sreg), .out(multiplexer_7_out), .sel(CROM[16:15]));
  // Probe on CROM[16:15]
  // Probe on cond
  LED led_2 (.in(CROM[19]));
  DotMatrix #(.inputtype("row"), .matrixcols(16), .matrixrows(16)) dotmatrix_1 (
    .row0(frame_buffer_16x16_1_out_21), .row1(frame_buffer_16x16_1_out_20),
    .row2(frame_buffer_16x16_1_out_19), .row3(frame_buffer_16x16_1_out_18),
    .row4(frame_buffer_16x16_1_out_17), .row5(frame_buffer_16x16_1_out_16),
    .row6(frame_buffer_16x16_1_out_15), .row7(frame_buffer_16x16_1_out_14),
    .row8(frame_buffer_16x16_1_out_13), .row9(frame_buffer_16x16_1_out_12),
    .row10(frame_buffer_16x16_1_out_11), .row11(frame_buffer_16x16_1_out_10),
    .row12(frame_buffer_16x16_1_out_9), .row13(frame_buffer_16x16_1_out_8),
    .row14(frame_buffer_16x16_1_out_7), .row15(frame_buffer_16x16_1_out_6));
  Button Clear (.out(Clear_out));
  Counters counters_1 (
    .new_ucounter(adder_1_out), .reset(reset), .clock(CLK), .cmds(cmds), .cycles(cycles), .icycles(icycles));
  // IntToFP #(.mode("unsigned"), .width(16)) inttofp_1: pin names not known; wires that end beside it: data, inttofp_1_p2
  Button u_Cont (.out(cont));
  // Probe on registerfile_1_r0
  // Probe on registerfile_1_r1
  // Probe on registerfile_1_r2
  // Probe on registerfile_1_r3
  // Probe on registerfile_1_r4
  // Probe on registerfile_1_r5
  // Probe on registerfile_1_r6
  // Probe on registerfile_1_r7
  Registerfile registerfile_1 (
    .dsel(dregs), .regval(multiplexer_7_out), .dwrite(CROM[12]), .ssel(sregs), .swrite(CROM[22]),
    .tsel(tregs), .twrite(twrite), .clock(CLK), .Reset(reset), .dreg(dreg), .sreg(sreg), .treg(treg),
    .r0(registerfile_1_r0), .r1(registerfile_1_r1), .r2(registerfile_1_r2), .r3(registerfile_1_r3),
    .r4(registerfile_1_r4), .r5(registerfile_1_r5), .r6(registerfile_1_r6), .r7(registerfile_1_r7));
  // Probe on tregs
  // Probe on sregs
  // Probe on dregs
  // Probe on CROM[16:15]
  LED led_3 (.in(CROM[14]));
  // Probe on inttofp_1_p2
  // Probe on dreg
  // Probe on sreg
  // Probe on treg
  // Probe on {CROM[31:19], cond, CROM[16:9], addrsel, CROM[6:4], aluop}
  LED led_4 (.in(CROM[12]));
  LED led_5 (.in(CROM[13]));
  Button clear_video (.out(clear_video_out));
  FPMultiplier fpmultiplier_1 (.a(32'h4380007f), .b(inttofp_1_p2), .out(fpmultiplier_1_out));
  // Probe on fpmultiplier_1_out
  // Probe on opcode
  // Probe on tregs
  Multiplexer #(.select(2), .width(16)) multiplexer_8 (
    .in0(treg), .in1(immed), .in2({16{1'b0}}), .in3(16'h1), .out(multiplexer_8_out), .sel(CROM[5:4]));
  // Probe on CROM[5:4]
  // Probe on CROM[10:9]
  LED led_6 (.in(CROM[11]));
  // RGB_Video #(.cursor("No Cursor")) rgb_video_1: pin names not known; wires that end beside it: Clear_out, clear_video_out, CLK, rgb_video_1_p4, address[13:7], address[6:0], rgb_video_1_p7
  and and_6 (rgb_video_1_p4, RGB_video, CROM[6]);
  // FPToInt #(.width(24)) fptoint_1: pin names not known; wires that end beside it: fpmultiplier_1_out, rgb_video_1_p7
  // Probe on rgb_video_1_p7
  // Probe on irreg
  // Probe on sregs
  // Probe on dregs
  DebugUnit debugunit_1 (
    .reset(reset), .\continue (cont), .clock(CLKIN), .pcreg(pcreg), .break_addr(Addr), .break_on_addr(Stop),
    .ucounter(ucounter), .break_on_instr(Instr), .break_on_cycle(Cycle), .clock_out(CLK));
  ALU alu_1 (.A(sreg), .B(multiplexer_8_out), .aluop(aluop), .Result(aluout), .Carry(c), .Zero(z), .Negative(n));
  // Probe on sreg
  // Probe on multiplexer_8_out
  // Probe on aluop
  // Probe on addrsel
  LED led_7 (.in(CROM[6]));
  // Probe on data[6:0]
  TTY #(.cols(16), .rows(4)) tty_1 (.data(data[6:0]), .clk(CLK), .we(and_7_out), .clr(Clear_Screen_out));
  and and_7 (and_7_out, TTYSel, CROM[6]);
  // Probe on address[13:7]
  // Probe on aluout
  // Probe on icycles
  // Probe on DROM
  // Probe on CROM[5:4]
  Button Clear_Screen (.out(Clear_Screen_out));
  // Probe on rgb_video_1_p7
  // Probe on address
  LED u_C (.in(c));
  LED u_Z (.in(z));
  LED u_N (.in(n));
  // Probe on cycles
  // Probe on aluop
  // Probe on address[6:0]
  // Probe on data
  // Probe on pcreg
  // Probe on irreg
  // Probe on immed
  // Probe on aluout
  LED New_CMD (.in(Ncmd));
  // Probe on cmds
  Button button_1 (.out(button_1_out));
  LED led_8 (.in(fswrite));
  // Probe on fsselADDR
  // RGB_Video #(.cursor("No Cursor"), .height(32), .scale(4), .width(32)) rgb_video_2: pin names not known; wires that end beside it: button_1_out, CLK, rgb_video_2_p3, address[9:5], address[4:0], data
  and and_8 (rgb_video_2_p3, RGB_video, CROM[6]);
  // Probe on address[9:5]
  // Probe on fpu_1_s0
  FPU fpu_1 (
    .data(data), .Reset(reset), .clock(CLK), .fswrite(fswrite), .fsselADDR(fsselADDR), .fpuenable(fpuenable),
    .s0(fpu_1_s0), .s1(fpu_1_s1), .s2(fpu_1_s2), .s3(fpu_1_s3), .NaNerror(fpu_1_nanerror), .s4(fpu_1_s4),
    .s5(fpu_1_s5), .s6(fpu_1_s6), .s7(fpu_1_s7), .s8(fpu_1_s8), .s9(fpu_1_s9), .s10(fpu_1_s10),
    .s11(fpu_1_s11), .s12(fpu_1_s12), .s13(fpu_1_s13), .Zero(fpu_1_zero), .s14(fpu_1_s14), .s15(fpu_1_s15),
    .fsreg(fsreg), .d0(fpu_1_d0), .d1(fpu_1_d1), .d2(fpu_1_d2), .d3(fpu_1_d3), .d4(fpu_1_d4), .d5(fpu_1_d5),
    .d6(fpu_1_d6), .d7(fpu_1_d7), .resultD0(fpu_1_resultd0), .resultD1(fpu_1_resultd1));
  // Probe on fpu_1_s1
  // Probe on fpu_1_s2
  // Probe on fpu_1_s3
  LED led_9 (.in(fpu_1_nanerror));
  // Probe on fpu_1_s4
  // Probe on fpu_1_s5
  // Probe on fpu_1_s6
  // Probe on fpu_1_s7
  // Probe on fpu_1_s8
  // Probe on fpu_1_s9
  // Probe on fpu_1_s10
  // Probe on fpu_1_s11
  // Probe on fpu_1_s12
  // Probe on fpu_1_s13
  LED led_10 (.in(fpu_1_zero));
  // Probe on fpu_1_s14
  // Probe on fpu_1_s15
  // Probe on fpu_1_d0
  // Probe on fpu_1_d1
  // Probe on fpu_1_d2
  // Probe on fpu_1_d3
  // Probe on fpu_1_d4
  // Probe on fpu_1_d5
  // Probe on fpu_1_d6
  // Probe on fpu_1_d7
  // Probe on data
  assign xor_1_out = opcode ^ 7'b1000001;  // XOR_Gate xor_1, 7 bits wide
  // Probe on {fpu_1_resultd1, fpu_1_resultd0}
  // Probe on address[4:0]
  nor nor_2 (isWrite, xor_1_out[0], xor_1_out[1], xor_1_out[2], xor_1_out[3], xor_1_out[4], xor_1_out[5], xor_1_out[6]);
  // Probe on fsreg

  // Other names for the same wires on the sheet: CROM (some bits) = {cond, addrsel, aluop}; op2sel[1:0] = CROM[5:4];
  //   datawrite = CROM[6]; pcsel[1:0] = CROM[10:9]; pcload = CROM[11]; dwrite = CROM[12]; irload = CROM[13];
  //   imload = CROM[14]; regsrc[1:0] = CROM[16:15]; indexsel = CROM[19]; datasel[1:0] = CROM[21:20];
  //   swrite = CROM[22]; dbgadr = Stop; dbgcyc = Cycle; dbgins = Instr; MicroPC[7:0] = ucounter

  // Notes on the sheet:
  //   Based on: http://minnie.tuhs.org/Programs/UcodeCPU/index.html
  //   v05: Migration to EVO, Debug, Counters, ImmReg Units
  //   v05a: norz instead of corz
  //   Address BUS
  //   RAM
  //   Control ROM
  //   Address of third uinstruction is "opcode+2"
  //   contents of rom_1 (hex, n*v repeats v):
  //   2000 80800 11000 11001 0 0 0 11005 11006 4*0 1100b 1100b 0 0 0 4*4000 0 4000 4000 0 0 0 4000 4000 0
  //   0 0 10*4000 4*0 4000 4000 4000 11*0 4000 4180 410030 410031 1000 4*4000 410031 1180 19000 0 0 1100
  //   100140 53*0 11010 11011 11012 11013 11015 11016 1101b 1101c 71000 71001 1 1 20001 20001 60001 60001
  //   21 21 1 1 800 410031 1c0 a00 410030 1080 1000c0 1110 100150 1001c0 410030 800 a00 c00
  //   contents of rom_2 (hex, n*v repeats v):
  //   101 202 16*0 8282 8383 8484 8585 0 8686 8787 0 0 0 8888 8989 0 0 0 8a8a 8b8b 8c8c 8d8d 8e8e 8f8f
  //   9090 9191 9292 9393 4*0 a2a2 9494 9595 11*0 9696 9999 0 0 a1a1 9b9b 9c9c 9d9d 9e9e 9f9f a0a0 58*0
  //   8*a1a1 a2a1 a2a1 a2a1 a1a2 a1a2 a2a1 a2a1 a1a2 a2a1 a1a2 a3a1 a1a3 9797 9898 a2a2 9a9a 0 4*a1a1
  //   MiMo - Microprogrammed CPU Model
  //   Microcode Control Unit
  //   Decision ROM
  //   Data BUS
  //   ImmReg
  //   v0.5a OR EVO
  //   Quick tips:
  //   Debug
  //   PC
  //   InsReg
  //   Use ctrl+t to manually toggle global clock signal
  //   Use Simulate->Ticks Enabled for automatic clock signal
  //   Registers
  //   Frame Buffer LED 16x16
  //   Micro Instruction
  //   Instruction:
  //   ALU
  //   TTY
  //   Address, Data Bus
  //   Spec. Registers
  //   Flags
  //   Status
  //   gets set to 1 if instruction is `sw`
endmodule

module InstructionReg (
  input  [15:0] instruction,
  input  reset,
  input  clock,
  input  irload,
  output [2:0] dregsel,
  output [2:0] sregsel,
  output [2:0] tregsel,
  output [6:0] opcode,
  output [15:0] Instruction_register_Content
);

  Register #(.width(16)) register_1 (
    .D(instruction), .en(irload), .Q({Instruction_register_Content[15:3], dregsel}), .clk(clock), .clr(reset));

  assign Instruction_register_Content[2:0] = dregsel;
  assign opcode = Instruction_register_Content[15:9];
  assign sregsel = Instruction_register_Content[5:3];
  assign tregsel = Instruction_register_Content[8:6];

  // Notes on the sheet:
  //   IR Logic
endmodule

module Registerfile (
  input  [15:0] regval,
  input  Reset,
  input  clock,
  input  dwrite,
  input  swrite,
  input  twrite,
  input  [2:0] dsel,
  input  [2:0] ssel,
  input  [2:0] tsel,
  output [15:0] r0,
  output [15:0] r1,
  output [15:0] r2,
  output [15:0] r3,
  output [15:0] r4,
  output [15:0] r5,
  output [15:0] r6,
  output [15:0] r7,
  output [15:0] dreg,
  output [15:0] sreg,
  output [15:0] treg
);

  wire demultiplexer_1_out0, demultiplexer_1_out1, demultiplexer_1_out2, demultiplexer_1_out3,
       demultiplexer_1_out4, demultiplexer_1_out5, demultiplexer_1_out6, demultiplexer_1_out7;

  Demultiplexer #(.select(3)) demultiplexer_1 (
    .out0(demultiplexer_1_out0), .out1(demultiplexer_1_out1), .out2(demultiplexer_1_out2),
    .out3(demultiplexer_1_out3), .out4(demultiplexer_1_out4), .out5(demultiplexer_1_out5),
    .out6(demultiplexer_1_out6), .out7(demultiplexer_1_out7), .in(dwrite), .sel(dsel));
  Demultiplexer #(.select(3)) demultiplexer_2 (
    .out0(demultiplexer_1_out0), .out1(demultiplexer_1_out1), .out2(demultiplexer_1_out2),
    .out3(demultiplexer_1_out3), .out4(demultiplexer_1_out4), .out5(demultiplexer_1_out5),
    .out6(demultiplexer_1_out6), .out7(demultiplexer_1_out7), .in(swrite), .sel(ssel));
  Demultiplexer #(.select(3)) demultiplexer_3 (
    .out0(demultiplexer_1_out0), .out1(demultiplexer_1_out1), .out2(demultiplexer_1_out2),
    .out3(demultiplexer_1_out3), .out4(demultiplexer_1_out4), .out5(demultiplexer_1_out5),
    .out6(demultiplexer_1_out6), .out7(demultiplexer_1_out7), .in(twrite), .sel(tsel));
  Register #(.width(16)) register_1 (.D(regval), .en(demultiplexer_1_out0), .Q(r0), .clk(clock), .clr(Reset));
  Register #(.width(16)) register_2 (.D(regval), .en(demultiplexer_1_out1), .Q(r1), .clk(clock), .clr(Reset));
  Register #(.width(16)) register_3 (.D(regval), .en(demultiplexer_1_out2), .Q(r2), .clk(clock), .clr(Reset));
  Register #(.width(16)) register_4 (.D(regval), .en(demultiplexer_1_out3), .Q(r3), .clk(clock), .clr(Reset));
  Register #(.width(16)) register_5 (.D(regval), .en(demultiplexer_1_out4), .Q(r4), .clk(clock), .clr(Reset));
  Register #(.width(16)) register_6 (.D(regval), .en(demultiplexer_1_out5), .Q(r5), .clk(clock), .clr(Reset));
  Register #(.width(16)) register_7 (.D(regval), .en(demultiplexer_1_out6), .Q(r6), .clk(clock), .clr(Reset));
  Register #(.width(16)) register_8 (.D(regval), .en(demultiplexer_1_out7), .Q(r7), .clk(clock), .clr(Reset));
  Multiplexer #(.select(3), .width(16)) multiplexer_1 (
    .in0(r0), .in1(r1), .in2(r2), .in3(r3), .in4(r4), .in5(r5), .in6(r6), .in7(r7), .out(dreg), .sel(dsel));
  Multiplexer #(.select(3), .width(16)) multiplexer_2 (
    .in0(r0), .in1(r1), .in2(r2), .in3(r3), .in4(r4), .in5(r5), .in6(r6), .in7(r7), .out(sreg), .sel(ssel));
  Multiplexer #(.select(3), .width(16)) multiplexer_3 (
    .in0(r0), .in1(r1), .in2(r2), .in3(r3), .in4(r4), .in5(r5), .in6(r6), .in7(r7), .out(treg), .sel(tsel));

  // Notes on the sheet:
  //   Register File
endmodule

module ALU (
  input  [15:0] A,
  input  [15:0] B,
  input  [3:0] aluop,
  output Carry,
  output Zero,
  output Negative,
  output [15:0] Result
);

  wire adder_1_cout, or_2_out, subtractor_1_bout;
  wire [15:0] adder_1_out, and_1_out, divider_1_out, divider_1_rem, multiplier_1_out, nand_1_out, nor_1_out,
       not_1_out, or_1_out, shifter_1_out, shifter_2_out, shifter_3_out, shifter_4_out, shifter_5_out,
       subtractor_1_out, xor_1_out;

  Adder #(.width(16)) adder_1 (.a(A), .b(B), .out(adder_1_out), .cin(1'b0), .cout(adder_1_cout));
  Subtractor #(.width(16)) subtractor_1 (.a(A), .b(B), .out(subtractor_1_out), .bin(1'b0), .bout(subtractor_1_bout));
  Multiplier #(.width(16)) multiplier_1 (.a(A), .b(B), .out(multiplier_1_out), .cin({16{1'b0}}));  // open: cout
  Divider #(.width(16)) divider_1 (.a(A), .b(B), .out(divider_1_out), .upper({16{1'b0}}), .rem(divider_1_rem));
  assign and_1_out = A & B;  // AND_Gate and_1, 16 bits wide
  assign or_1_out = A | B;  // OR_Gate or_1, 16 bits wide
  assign xor_1_out = A ^ B;  // XOR_Gate xor_1, 16 bits wide
  assign nand_1_out = ~(A & B);  // NAND_Gate nand_1, 16 bits wide
  assign nor_1_out = ~(A | B);  // NOR_Gate nor_1, 16 bits wide
  assign not_1_out = ~A;  // NOT_Gate not_1, 16 bits wide
  Shifter #(.width(16)) shifter_1 (.in(A), .\dist (B[3:0]), .out(shifter_1_out));
  Shifter #(.shift("lr"), .width(16)) shifter_2 (.in(A), .\dist (B[3:0]), .out(shifter_2_out));
  Shifter #(.shift("ar"), .width(16)) shifter_3 (.in(A), .\dist (B[3:0]), .out(shifter_3_out));
  Shifter #(.shift("rl"), .width(16)) shifter_4 (.in(A), .\dist (B[3:0]), .out(shifter_4_out));
  Shifter #(.shift("rr"), .width(16)) shifter_5 (.in(A), .\dist (B[3:0]), .out(shifter_5_out));
  Multiplexer #(.select(4), .width(16)) multiplexer_1 (
    .in0(adder_1_out), .in1(subtractor_1_out), .in2(multiplier_1_out), .in3(divider_1_out),
    .in4(divider_1_rem), .in5(and_1_out), .in6(or_1_out), .in7(xor_1_out), .in8(nand_1_out), .in9(nor_1_out),
    .in10(not_1_out), .in11(shifter_1_out), .in12(shifter_2_out), .in13(shifter_3_out), .in14(shifter_4_out),
    .in15(shifter_5_out), .out({Negative, Result[14:0]}), .sel(aluop));
  Multiplexer #(.select(4)) multiplexer_2 (
    .in0(adder_1_cout), .in1(subtractor_1_bout), .in2(1'b0), .in3(1'b0), .in4(1'b0), .in5(1'b0), .in6(1'b0),
    .in7(1'b0), .in8(1'b0), .in9(1'b0), .in10(1'b0), .in11(1'b0), .in12(1'b0), .in13(1'b0), .in14(1'b0),
    .in15(1'b0), .out(Carry), .sel(aluop));
  or or_2 (or_2_out, Result[0], Result[1], Result[2], Result[3], Result[4], Result[5], Result[6], Result[7], Result[9], Result[10], Result[11], Result[12], Result[13], Result[14], Negative, Result[8]);
  not not_2 (Zero, or_2_out);

  assign Result[15] = Negative;

  // Notes on the sheet:
  //   16-bit ALU
endmodule

module PC (
  input  [15:0] imreg,
  input  pcload,
  input  clock,
  input  reset,
  input  [15:0] sreg,
  input  [1:0] pcsel,
  output [15:0] pcout
);

  wire [15:0] adder_1_out, adder_2_out, multiplexer_1_out;

  Adder #(.width(16)) adder_1 (.a(pcout), .b(16'h1), .out(adder_1_out));  // open: cin, cout
  Adder #(.width(16)) adder_2 (.a(pcout), .b(imreg), .out(adder_2_out));  // open: cin, cout
  Multiplexer #(.select(2), .width(16)) multiplexer_1 (
    .in0(adder_1_out), .in1(imreg), .in2(adder_2_out), .in3(sreg), .out(multiplexer_1_out), .sel(pcsel));
  Register #(.width(16)) register_1 (.D(multiplexer_1_out), .en(pcload), .Q(pcout), .clk(clock), .clr(reset));

  // Notes on the sheet:
  //   PC Logic
endmodule

module ShowHexa (
  input  [15:0] Data,
  output [3:0] out_2,
  output [3:0] out_3,
  output [3:0] Digit,
  output [3:0] out_5
);


  assign Digit = Data[7:4];
  assign out_2 = Data[15:12];
  assign out_3 = Data[11:8];
  assign out_5 = Data[3:0];
endmodule

module Frame_Buffer_16x16 (
  input  [3:0] address,
  input  store,
  input  [15:0] data,
  input  clock,
  input  reset,
  output [15:0] out_6,
  output [15:0] out_7,
  output [15:0] out_8,
  output [15:0] out_9,
  output [15:0] out_10,
  output [15:0] out_11,
  output [15:0] out_12,
  output [15:0] out_13,
  output [15:0] out_14,
  output [15:0] out_15,
  output [15:0] out_16,
  output [15:0] out_17,
  output [15:0] out_18,
  output [15:0] out_19,
  output [15:0] out_20,
  output [15:0] out_21
);

  wire demultiplexer_1_out0, demultiplexer_1_out1, demultiplexer_1_out2, demultiplexer_1_out3,
       demultiplexer_1_out4, demultiplexer_1_out5, demultiplexer_1_out6, demultiplexer_1_out7,
       demultiplexer_1_out8, demultiplexer_1_out9, demultiplexer_1_out10, demultiplexer_1_out11,
       demultiplexer_1_out12, demultiplexer_1_out13, demultiplexer_1_out14, demultiplexer_1_out15;

  Demultiplexer #(.select(4)) demultiplexer_1 (
    .out0(demultiplexer_1_out0), .out1(demultiplexer_1_out1), .out2(demultiplexer_1_out2),
    .out3(demultiplexer_1_out3), .out4(demultiplexer_1_out4), .out5(demultiplexer_1_out5),
    .out6(demultiplexer_1_out6), .out7(demultiplexer_1_out7), .out8(demultiplexer_1_out8),
    .out9(demultiplexer_1_out9), .out10(demultiplexer_1_out10), .out11(demultiplexer_1_out11),
    .out12(demultiplexer_1_out12), .out13(demultiplexer_1_out13), .out14(demultiplexer_1_out14),
    .out15(demultiplexer_1_out15), .in(store), .sel(address));
  Register #(.width(16)) register_1 (.D(data), .en(demultiplexer_1_out0), .Q(out_6), .clk(clock), .clr(reset));
  Register #(.width(16)) register_2 (.D(data), .en(demultiplexer_1_out1), .Q(out_7), .clk(clock), .clr(reset));
  Register #(.width(16)) register_3 (.D(data), .en(demultiplexer_1_out2), .Q(out_8), .clk(clock), .clr(reset));
  Register #(.width(16)) register_4 (.D(data), .en(demultiplexer_1_out3), .Q(out_9), .clk(clock), .clr(reset));
  Register #(.width(16)) register_5 (.D(data), .en(demultiplexer_1_out4), .Q(out_10), .clk(clock), .clr(reset));
  Register #(.width(16)) register_6 (.D(data), .en(demultiplexer_1_out5), .Q(out_11), .clk(clock), .clr(reset));
  Register #(.width(16)) register_7 (.D(data), .en(demultiplexer_1_out6), .Q(out_12), .clk(clock), .clr(reset));
  Register #(.width(16)) register_8 (.D(data), .en(demultiplexer_1_out7), .Q(out_13), .clk(clock), .clr(reset));
  Register #(.width(16)) register_9 (.D(data), .en(demultiplexer_1_out8), .Q(out_14), .clk(clock), .clr(reset));
  Register #(.width(16)) register_10 (.D(data), .en(demultiplexer_1_out9), .Q(out_15), .clk(clock), .clr(reset));
  Register #(.width(16)) register_11 (.D(data), .en(demultiplexer_1_out10), .Q(out_16), .clk(clock), .clr(reset));
  Register #(.width(16)) register_12 (.D(data), .en(demultiplexer_1_out11), .Q(out_17), .clk(clock), .clr(reset));
  Register #(.width(16)) register_13 (.D(data), .en(demultiplexer_1_out12), .Q(out_18), .clk(clock), .clr(reset));
  Register #(.width(16)) register_14 (.D(data), .en(demultiplexer_1_out13), .Q(out_19), .clk(clock), .clr(reset));
  Register #(.width(16)) register_15 (.D(data), .en(demultiplexer_1_out14), .Q(out_20), .clk(clock), .clr(reset));
  Register #(.width(16)) register_16 (.D(data), .en(demultiplexer_1_out15), .Q(out_21), .clk(clock), .clr(reset));
endmodule

module Address_Decoder (
  input  enable,
  input  [15:0] Address,
  output RAM,
  output FB_LED,
  output RGB_video,
  output [3:0] fssel,
  output fswrite,
  output fpuenable,
  output TTY
);

  wire comparator_1_eq, comparator_1_gt, comparator_1_lt, decoder_1_out2;

  Decoder #(.select(2)) decoder_1 (
    .out0(RAM), .out1(FB_LED), .out2(decoder_1_out2), .out3(RGB_video), .sel(Address[15:14]), .en(enable));
  Comparator #(.width(14)) comparator_1 (
    .a(Address[13:0]), .b(14'h10), .gt(comparator_1_gt), .eq(comparator_1_eq), .lt(comparator_1_lt));
  and and_1 (fswrite, decoder_1_out2, comparator_1_lt);
  and and_2 (fpuenable, decoder_1_out2, comparator_1_eq);
  and and_3 (TTY, decoder_1_out2, comparator_1_gt);

  assign fssel = Address[3:0];
endmodule

module Counters (
  input  [7:0] new_ucounter,
  input  reset,
  input  clock,
  output [15:0] cycles,
  output [3:0] icycles,
  output [15:0] cmds
);

  wire nor_1_out;

  nor nor_1 (nor_1_out, new_ucounter[7], new_ucounter[6], new_ucounter[5], new_ucounter[4], new_ucounter[2], new_ucounter[1], new_ucounter[0], new_ucounter[3]);
  Counter #(.max('hffff), .width(16)) counter_1 (
    .Q(cycles), .clk(clock), .clr(reset));  // open: load, D, count, carry, up
  Counter #(.max('hf), .width(4)) counter_2 (
    .load(nor_1_out), .D(4'b0000), .Q(icycles), .clk(clock), .clr(reset));  // open: count, carry, up
  Counter #(.max('hffff), .width(16)) counter_3 (
    .count(nor_1_out), .Q(cmds), .clk(clock), .clr(reset));  // open: load, D, carry, up
  // Probe on cycles
  // Probe on icycles
  // Probe on cmds

  // Notes on the sheet:
  //   Counts the number of clock cycles
  //   since the start.
  //   Counts the number of clock cycles
  //   since the start of current instruction.
  //   Counts the number of instructions
  //   since the start.
  //   Cycle/Cmds Counters
endmodule

module DebugUnit (
  input  reset,
  input  \continue ,
  input  clock,
  input  [15:0] pcreg,
  input  [15:0] break_addr,
  input  break_on_addr,
  input  [7:0] ucounter,
  input  break_on_instr,
  input  break_on_cycle,
  output clock_out
);

  wire and_1_out, and_2_out, and_3_out, nor_1_out, nor_2_out, nor_3_out, or_1_out, shift_register_1_out,
       shift_register_1_q0;
  wire [15:0] xor_1_out;

  Shift_Register #(.length(2), .trigger("falling")) shift_register_1 (
    .in(\continue ), .clk(clock), .out(shift_register_1_out), .clr(reset), .q0(shift_register_1_q0));  // open: shift, load, d0, d1, q1
  assign xor_1_out = pcreg ^ break_addr;  // XOR_Gate xor_1, 16 bits wide
  LED Addr (.in(break_on_addr));
  and and_1 (and_1_out, ~shift_register_1_out, shift_register_1_q0);  // AND_Gate
  nor nor_1 (nor_1_out, xor_1_out[15], xor_1_out[14], xor_1_out[13], xor_1_out[12], xor_1_out[11], xor_1_out[10], xor_1_out[9], xor_1_out[8], xor_1_out[6], xor_1_out[5], xor_1_out[4], xor_1_out[3], xor_1_out[2], xor_1_out[1], xor_1_out[0], xor_1_out[7]);
  and and_2 (and_2_out, nor_1_out, break_on_addr, nor_2_out);
  nor nor_2 (nor_2_out, ucounter[7], ucounter[6], ucounter[5], ucounter[4], ucounter[2], ucounter[1], ucounter[0], ucounter[3]);
  and and_3 (and_3_out, nor_2_out, break_on_instr);
  LED Instr (.in(break_on_instr));
  LED Cycle (.in(break_on_cycle));
  nor nor_3 (nor_3_out, and_2_out, and_3_out, break_on_cycle);
  or or_1 (or_1_out, and_1_out, nor_3_out);
  LED Pass (.in(or_1_out));
  and and_4 (clock_out, clock, or_1_out);

  // Notes on the sheet:
  //   Breaks on PC = break_addr
  //   Breaks on each new instruction
  //   Breaks on each clock pulse
  //   Makes sure the 'continue' button only
  //   lets through 1 clock pulse, until you let go
  //   and press it again.
  //   Outputs 1 only on first cycle (shift bits are unequal).
  //   Debug Unit
  //   PC = break_addr?
endmodule

module ImmediateReg (
  input  [15:0] DataIn,
  input  IMLoad,
  input  CLKin,
  output [15:0] ImmOut
);

  Register #(.width(16)) register_1 (.D(DataIn), .en(IMLoad), .Q(ImmOut), .clk(CLKin));  // open: clr
  // Probe on ImmOut
endmodule

module FPU (
  input  [15:0] data,
  input  Reset,
  input  clock,
  input  fswrite,
  input  [3:0] fsselADDR,
  input  fpuenable,
  output [15:0] s0,
  output [15:0] s1,
  output [15:0] s2,
  output [15:0] s3,
  output NaNerror,
  output [15:0] s4,
  output [15:0] s5,
  output [15:0] s6,
  output [15:0] s7,
  output [15:0] s8,
  output [15:0] s9,
  output [15:0] s10,
  output [15:0] s11,
  output [15:0] s12,
  output [15:0] s13,
  output Zero,
  output [15:0] s14,
  output [15:0] s15,
  output [15:0] fsreg,
  output [31:0] d0,
  output [31:0] d1,
  output [31:0] d2,
  output [31:0] d3,
  output [31:0] d4,
  output [31:0] d5,
  output [31:0] d6,
  output [31:0] d7,
  output [15:0] resultD0,
  output [15:0] resultD1
);

  wire and_2_out, and_3_out, and_4_out, demultiplexer_1_out0, demultiplexer_1_out1, demultiplexer_1_out2,
       demultiplexer_1_out3, demultiplexer_1_out4, demultiplexer_1_out5, demultiplexer_1_out6,
       demultiplexer_1_out7, demultiplexer_1_out8, demultiplexer_1_out9, demultiplexer_1_out10,
       demultiplexer_1_out11, demultiplexer_1_out12, demultiplexer_1_out13, demultiplexer_1_out14,
       demultiplexer_1_out15, not_1_out, not_2_out, or_1_out, or_2_out, or_3_out, resultwrite, undriven,
       undriven_2, undriven_3, undriven_4, undriven_5, undriven_6;
  wire [3:0] multiplexer_2_out, multiplexer_3_out;
  wire [15:0] fdreg, fpadder_2_out, fpadder_4_out, fpdivider_2_out, fpmultiplier_3_out, fpmultiplier_4_out,
       fpsubtractor_2_out, ftreg, multiplexer_1_out, result;
  wire [31:0] fdregD, fpadder_1_out, fpadder_3_out, fpdivider_1_out, fpmultiplier_1_out, fpmultiplier_2_out,
       fpmultiplier_5_out, fpmultiplier_6_out, fpmultiplier_7_out, fpmultiplier_8_out, fpsubtractor_1_out,
       fpsubtractor_3_out, fsregD, ftregD, multiplexer_12_out, shifter_1_out, y;

  and and_1 (resultwrite, fpuenable, not_1_out);
  not not_1 (not_1_out, data[15]);
  Multiplexer #(.width(16)) multiplexer_1 (.in0(data), .in1(result), .out(multiplexer_1_out), .sel(resultwrite));
  Multiplexer #(.width(4)) multiplexer_2 (
    .in0(fsselADDR), .in1(data[11:8]), .out(multiplexer_2_out), .sel(resultwrite));
  Demultiplexer #(.select(4)) demultiplexer_1 (
    .out0(demultiplexer_1_out0), .out1(demultiplexer_1_out1), .out2(demultiplexer_1_out2),
    .out3(demultiplexer_1_out3), .out4(demultiplexer_1_out4), .out5(demultiplexer_1_out5),
    .out6(demultiplexer_1_out6), .out7(demultiplexer_1_out7), .out8(demultiplexer_1_out8),
    .out9(demultiplexer_1_out9), .out10(demultiplexer_1_out10), .out11(demultiplexer_1_out11),
    .out12(demultiplexer_1_out12), .out13(demultiplexer_1_out13), .out14(demultiplexer_1_out14),
    .out15(demultiplexer_1_out15), .in(or_1_out), .sel(multiplexer_2_out));
  or or_1 (or_1_out, fswrite, resultwrite);
  Register #(.width(16)) register_1 (
    .D(multiplexer_1_out), .en(demultiplexer_1_out0), .Q(d0[15:0]), .clk(clock), .clr(Reset));
  Register #(.width(16)) register_2 (
    .D(multiplexer_1_out), .en(demultiplexer_1_out1), .Q(d0[31:16]), .clk(clock), .clr(Reset));
  Register #(.width(16)) register_3 (
    .D(multiplexer_1_out), .en(demultiplexer_1_out2), .Q(d1[15:0]), .clk(clock), .clr(Reset));
  Register #(.width(16)) register_4 (
    .D(multiplexer_1_out), .en(demultiplexer_1_out3), .Q(d1[31:16]), .clk(clock), .clr(Reset));
  Register #(.width(16)) register_5 (
    .D(multiplexer_1_out), .en(demultiplexer_1_out4), .Q(d2[15:0]), .clk(clock), .clr(Reset));
  Register #(.width(16)) register_6 (
    .D(multiplexer_1_out), .en(demultiplexer_1_out5), .Q(d2[31:16]), .clk(clock), .clr(Reset));
  Register #(.width(16)) register_7 (
    .D(multiplexer_1_out), .en(demultiplexer_1_out6), .Q(d3[15:0]), .clk(clock), .clr(Reset));
  Register #(.width(16)) register_8 (
    .D(multiplexer_1_out), .en(demultiplexer_1_out7), .Q(d3[31:16]), .clk(clock), .clr(Reset));
  Register #(.width(16)) register_9 (
    .D(multiplexer_1_out), .en(demultiplexer_1_out8), .Q(d4[15:0]), .clk(clock), .clr(Reset));
  Register #(.width(16)) register_10 (
    .D(multiplexer_1_out), .en(demultiplexer_1_out9), .Q(d4[31:16]), .clk(clock), .clr(Reset));
  Register #(.width(16)) register_11 (
    .D(multiplexer_1_out), .en(demultiplexer_1_out10), .Q(d5[15:0]), .clk(clock), .clr(Reset));
  Register #(.width(16)) register_12 (
    .D(multiplexer_1_out), .en(demultiplexer_1_out11), .Q(d5[31:16]), .clk(clock), .clr(Reset));
  Register #(.width(16)) register_13 (
    .D(multiplexer_1_out), .en(demultiplexer_1_out12), .Q(d6[15:0]), .clk(clock), .clr(Reset));
  Register #(.width(16)) register_14 (
    .D(multiplexer_1_out), .en(demultiplexer_1_out13), .Q(d6[31:16]), .clk(clock), .clr(Reset));
  Register #(.width(16)) register_15 (
    .D(multiplexer_1_out), .en(demultiplexer_1_out14), .Q(d7[15:0]), .clk(clock), .clr(Reset));
  Register #(.width(16)) register_16 (
    .D(multiplexer_1_out), .en(demultiplexer_1_out15), .Q(d7[31:16]), .clk(clock), .clr(Reset));
  Multiplexer #(.width(4)) multiplexer_3 (.in0(fsselADDR), .in1(data[3:0]), .out(multiplexer_3_out), .sel(fpuenable));
  Multiplexer #(.select(4), .width(16)) multiplexer_4 (
    .in0(d0[15:0]), .in1(d0[31:16]), .in2(d1[15:0]), .in3(d1[31:16]), .in4(d2[15:0]), .in5(d2[31:16]),
    .in6(d3[15:0]), .in7(d3[31:16]), .in8(d4[15:0]), .in9(d4[31:16]), .in10(d5[15:0]), .in11(d5[31:16]),
    .in12(d6[15:0]), .in13(d6[31:16]), .in14(resultD0), .in15(resultD1), .out(fsreg), .sel(multiplexer_3_out));
  Multiplexer #(.enable("true"), .select(4), .width(32)) multiplexer_5 (
    .in0(d0), .in1(d1), .in2(d2), .in3(d3), .in4(d4), .in5(d5), .in6(d6), .in7(d7), .out(fsregD),
    .sel(data[3:0]), .en(data[15]));  // open: in8, in9, in10, in11, in12, in13, in14, in15
  Multiplexer #(.select(4), .width(16)) multiplexer_6 (
    .in0(d0[15:0]), .in1(d0[31:16]), .in2(d1[15:0]), .in3(d1[31:16]), .in4(d2[15:0]), .in5(d2[31:16]),
    .in6(d3[15:0]), .in7(d3[31:16]), .in8(d4[15:0]), .in9(d4[31:16]), .in10(d5[15:0]), .in11(d5[31:16]),
    .in12(d6[15:0]), .in13(d6[31:16]), .in14(d7[15:0]), .in15(d7[31:16]), .out(ftreg), .sel(data[7:4]));
  Multiplexer #(.enable("true"), .select(4), .width(32)) multiplexer_7 (
    .in0(d0), .in1(d1), .in2(d2), .in3(d3), .in4(d4), .in5(d5), .in6(d6), .in7(d7), .out(ftregD),
    .sel(data[7:4]), .en(data[15]));  // open: in8, in9, in10, in11, in12, in13, in14, in15
  Multiplexer #(.select(4), .width(16)) multiplexer_8 (
    .in0(d0[15:0]), .in1(d0[31:16]), .in2(d1[15:0]), .in3(d1[31:16]), .in4(d2[15:0]), .in5(d2[31:16]),
    .in6(d3[15:0]), .in7(d3[31:16]), .in8(d4[15:0]), .in9(d4[31:16]), .in10(d5[15:0]), .in11(d5[31:16]),
    .in12(d6[15:0]), .in13(d6[31:16]), .in14(d7[15:0]), .in15(d7[31:16]), .out(fdreg), .sel(data[11:8]));
  Multiplexer #(.enable("true"), .select(4), .width(32)) multiplexer_9 (
    .in0(d0), .in1(d1), .in2(d2), .in3(d3), .in4(d4), .in5(d5), .in6(d6), .in7(d7), .out(fdregD),
    .sel(data[11:8]), .en(data[15]));  // open: in8, in9, in10, in11, in12, in13, in14, in15
  FPAdder fpadder_1 (.a(fsregD), .b(ftregD), .out(fpadder_1_out));
  FPSubtractor fpsubtractor_1 (.a(fsregD), .b(ftregD), .out(fpsubtractor_1_out));
  FPMultiplier fpmultiplier_1 (.a(fsregD), .b(ftregD), .out(fpmultiplier_1_out));
  FPDivider fpdivider_1 (.a(fsregD), .b(ftregD), .out(fpdivider_1_out));
  FPMultiplier fpmultiplier_2 (.a(fsregD), .b(ftregD), .out(fpmultiplier_2_out));
  Shifter #(.shift("lr"), .width(32)) shifter_1 (.in(fsregD), .\dist (5'b00001), .out(shifter_1_out));
  FPAdder #(.fpwidth(16)) fpadder_2 (.a(fsreg), .b(ftreg), .out(fpadder_2_out));
  FPSubtractor #(.fpwidth(16)) fpsubtractor_2 (.a(fsreg), .b(ftreg), .out(fpsubtractor_2_out));
  FPMultiplier #(.fpwidth(16)) fpmultiplier_3 (.a(fsreg), .b(ftreg), .out(fpmultiplier_3_out));
  FPDivider #(.fpwidth(16)) fpdivider_2 (.a(fsreg), .b(ftreg), .out(fpdivider_2_out));
  FPMultiplier #(.fpwidth(16)) fpmultiplier_4 (.a(fsreg), .b(ftreg), .out(fpmultiplier_4_out));
  FPAdder fpadder_3 (.a(fpmultiplier_2_out), .b(fdregD), .out(fpadder_3_out));
  Subtractor #(.width(32)) subtractor_1 (.a(32'h5f3759df), .b(shifter_1_out), .out(y));  // open: bin, bout
  FPAdder #(.fpwidth(16)) fpadder_4 (.a(fpmultiplier_4_out), .b(fdreg), .out(fpadder_4_out));
  // Probe on data[14:12]
  FPMultiplier fpmultiplier_5 (.a(fsregD), .b(32'h3f000000), .out(fpmultiplier_5_out));
  and and_2 (and_2_out, not_2_out, fpuenable);
  not not_2 (not_2_out, data[15]);
  FPMultiplier fpmultiplier_6 (.a(fpmultiplier_5_out), .b(y), .out(fpmultiplier_6_out));
  Multiplexer #(.enable("true"), .select(3), .width(16)) multiplexer_10 (
    .in0(fpadder_2_out), .in1(fpsubtractor_2_out), .in2(fpmultiplier_3_out), .in3(fpdivider_2_out),
    .in4(fpadder_4_out), .out(result), .sel(data[14:12]), .en(and_2_out));  // open: in5, in6, in7
  FPMultiplier fpmultiplier_7 (.a(fpmultiplier_6_out), .b(y), .out(fpmultiplier_7_out));
  FPSubtractor fpsubtractor_3 (.a(32'h3fc00000), .b(fpmultiplier_7_out), .out(fpsubtractor_3_out));
  or or_2 (or_2_out, undriven_5, undriven_6);
  or or_3 (or_3_out, result[0], result[1], result[2], result[3], result[4], result[5], result[6], result[7], result[9], result[10], result[11], result[12], result[13], result[14], result[15], result[8]);
  FPMultiplier fpmultiplier_8 (.a(fpsubtractor_3_out), .b(y), .out(fpmultiplier_8_out));
  Multiplexer #(.select(3)) multiplexer_11 (
    .in0(undriven), .in1(undriven_2), .in2(undriven_3), .in3(undriven_4), .in4(or_2_out), .out(NaNerror),
    .sel(data[14:12]));  // open: in5, in6, in7
  not not_3 (Zero, or_3_out);
  // Probe on data[14:12]
  and and_3 (and_3_out, data[15], fpuenable);
  Multiplexer #(.enable("true"), .select(3), .width(32)) multiplexer_12 (
    .in0(fpadder_1_out), .in1(fpsubtractor_1_out), .in2(fpmultiplier_1_out), .in3(fpdivider_1_out),
    .in4(fpadder_3_out), .in5(fpmultiplier_8_out), .out(multiplexer_12_out), .sel(data[14:12]), .en(and_3_out));  // open: in6, in7
  and and_4 (and_4_out, fpuenable, data[15]);
  Register #(.width(16)) register_17 (
    .D(multiplexer_12_out[15:0]), .en(and_4_out), .Q(resultD0), .clk(clock), .clr(Reset));
  Register #(.width(16)) register_18 (
    .D(multiplexer_12_out[31:16]), .en(and_4_out), .Q(resultD1), .clk(clock), .clr(Reset));

  assign s0 = d0[15:0];
  assign s1 = d0[31:16];
  assign s2 = d1[15:0];
  assign s3 = d1[31:16];
  assign s4 = d2[15:0];
  assign s5 = d2[31:16];
  assign s6 = d3[15:0];
  assign s7 = d3[31:16];
  assign s8 = d4[15:0];
  assign s9 = d4[31:16];
  assign s10 = d5[15:0];
  assign s11 = d5[31:16];
  assign s12 = d6[15:0];
  assign s13 = d6[31:16];
  assign s14 = d7[15:0];
  assign s15 = d7[31:16];

  // Other names for the same wires on the sheet: fsselDATA[3:0] = data[3:0]; ftsel[3:0] = data[7:4];
  //   fdsel[3:0] = data[11:8]; fpuop[2:0] = data[14:12]; dmode = data[15]

  // Notes on the sheet:
  //   i
  //   0.5
  //   x2
  //   1.5
  //   x2 * y * y
endmodule
